// Logisim project cpu.circ as structural Verilog: 1 circuit, main circuit main
module main (
);

  wire and_1_out, and_2_out, decoder_1_out0, decoder_1_out1, decoder_1_out2, decoder_1_out3, decoder_1_out5,
       decoder_1_out6, decoder_1_out8, decoder_2_out0, decoder_2_out1, decoder_2_out4, decoder_3_out0,
       decoder_3_out1, decoder_3_out2, decoder_3_out3, decoder_3_out5, decoder_3_out8, MEM_CLK, MEM_O_EN,
       not_1_out, or_1_out, or_2_out, or_3_out, or_4_out, or_5_out, or_6_out, or_7_out, or_8_out, undriven;
  wire [3:0] counter_1_q, rom_1_data, rom_1_data_2;
  wire [7:0] ACC_H_q, ACC_L_q, controlled_buffer_1_out, controlled_buffer_1_out_2, controlled_buffer_3_out,
       DATA, DATA_LATCH_H_q, DATA_LATCH_L_q, demultiplexer_1_out0, demultiplexer_1_out1, multiplexer_2_out,
       multiplexer_4_out, multiplexer_5_out, OPCODE_LATCH_q, rom_1_data_3;
  wire [15:0] adder_1_out, BASE_q, IP_q, multiplexer_1_out, shift_register_2_p1;
  wire [15:2] multiplexer_3_out;

  // Shift_Register shift_register_1: pin names not known; wires that end beside it: shift_register_2_p1[1], shift_register_2_p1[3], shift_register_2_p1[5], shift_register_2_p1[7], shift_register_2_p1[9], shift_register_2_p1[11], shift_register_2_p1[13], shift_register_2_p1[15]
  // Shift_Register shift_register_2: pin names not known; wires that end beside it: shift_register_2_p1[0], shift_register_2_p1[2], shift_register_2_p1[4], shift_register_2_p1[6], shift_register_2_p1[8], shift_register_2_p1[10], shift_register_2_p1[12], shift_register_2_p1[14]
  Register #(.width(16)) BASE (
    .D({controlled_buffer_1_out_2, controlled_buffer_1_out}), .en(decoder_3_out8),
    .clk(shift_register_2_p1[0]), .Q(BASE_q));  // open: clr
  assign {controlled_buffer_1_out_2, controlled_buffer_1_out} = decoder_1_out8 ? BASE_q : 16'bz;  // Controlled_Buffer controlled_buffer_1
  Register #(.width(16)) IP (.D(multiplexer_1_out), .en(or_1_out), .clk(or_2_out), .Q(IP_q));  // open: clr
  Multiplexer #(.width(16)) multiplexer_1 (
    .in0({controlled_buffer_1_out_2, controlled_buffer_1_out}), .in1(adder_1_out), .out(multiplexer_1_out),
    .sel(decoder_2_out0));
  or or_1 (or_1_out, decoder_2_out0, decoder_3_out5);
  or or_2 (or_2_out, shift_register_2_p1[0], shift_register_2_p1[0]);
  assign {controlled_buffer_1_out_2, controlled_buffer_1_out} = decoder_1_out5 ? IP_q : 16'bz;  // Controlled_Buffer controlled_buffer_2
  Adder #(.width(16)) adder_1 (.a(IP_q), .out(adder_1_out));  // open: b, cin, cout
  Counter #(.max('hf), .width(4)) counter_1 (.Q(counter_1_q));  // open: clr, load, up, count, clk, D, carry
  Register OPCODE_LATCH (
    .D(controlled_buffer_1_out), .en(decoder_1_out6), .clk(shift_register_2_p1[0]), .Q(OPCODE_LATCH_q));  // open: clr
  ROM #(.addrWidth(12), .dataWidth(16)) rom_1 (
    .addr({OPCODE_LATCH_q, counter_1_q}), .data({rom_1_data_2, rom_1_data, rom_1_data_3}));
  Decoder #(.select(4)) decoder_1 (
    .out0(decoder_1_out0), .out1(decoder_1_out1), .out2(decoder_1_out2), .out3(decoder_1_out3),
    .out5(decoder_1_out5), .out6(decoder_1_out6), .out8(decoder_1_out8), .sel(rom_1_data), .en(decoder_2_out1));  // open: out4, out7, out9, out10, out11, out12, out13, out14, out15
  Multiplexer #(.width(8)) multiplexer_2 (
    .in0(controlled_buffer_1_out), .in1(controlled_buffer_1_out_2), .out(multiplexer_2_out),
    .sel(decoder_3_out2));
  or or_3 (or_3_out, decoder_3_out0, decoder_3_out2);
  Register ACC_L (.D(controlled_buffer_1_out), .en(or_3_out), .clk(shift_register_2_p1[0]), .Q(ACC_L_q));  // open: clr
  Register ACC_H (.D(multiplexer_2_out), .en(or_4_out), .clk(shift_register_2_p1[0]), .Q(ACC_H_q));  // open: clr
  or or_4 (or_4_out, decoder_3_out1, decoder_3_out2);
  Decoder #(.enable("false"), .select(4)) decoder_2 (
    .out0(decoder_2_out0), .out1(decoder_2_out1), .out4(decoder_2_out4), .sel(rom_1_data_3[3:0]));  // open: out2, out3, out5, out6, out7, out8, out9, out10, out11, out12, out13, out14, out15
  not not_1 (not_1_out, decoder_1_out1);
  Demultiplexer #(.width(8)) demultiplexer_1 (
    .out0(demultiplexer_1_out0), .out1(demultiplexer_1_out1), .in(ACC_H_q), .sel(decoder_1_out2));
  Decoder #(.select(4)) decoder_3 (
    .out0(decoder_3_out0), .out1(decoder_3_out1), .out2(decoder_3_out2), .out3(decoder_3_out3),
    .out5(decoder_3_out5), .out8(decoder_3_out8), .sel(rom_1_data_2));  // open: out4, out6, out7, out9, out10, out11, out12, out13, out14, out15, en
  assign controlled_buffer_3_out = not_1_out ? ACC_L_q : 8'bz;  // Controlled_Buffer controlled_buffer_3
  assign controlled_buffer_3_out = decoder_1_out1 ? demultiplexer_1_out0 : 8'bz;  // Controlled_Buffer controlled_buffer_4
  Register #(.width(16)) ADDR_LATCH ();  // open: D, en, clk, Q, clr
  assign {controlled_buffer_1_out_2, controlled_buffer_1_out} = or_5_out ? {demultiplexer_1_out1, controlled_buffer_3_out} : 16'bz;  // Controlled_Buffer controlled_buffer_5
  or or_5 (or_5_out, decoder_1_out0, decoder_1_out1, decoder_1_out2);
  or or_6 (or_6_out, undriven, and_1_out);
  and and_1 (and_1_out, MEM_CLK, multiplexer_3_out[3]);
  or or_7 (or_7_out, undriven, and_2_out);
  and and_2 (and_2_out, ~multiplexer_3_out[3], MEM_CLK);  // AND_Gate
  Multiplexer #(.width(16)) multiplexer_3 (
    .in0({16{1'b0}}), .in1(shift_register_2_p1), .out({multiplexer_3_out, MEM_CLK, MEM_O_EN}));  // open: sel
  Register DATA_LATCH_L (.D(controlled_buffer_1_out), .en(or_7_out), .clk(or_8_out), .Q(DATA_LATCH_L_q));  // open: clr
  Register DATA_LATCH_H (
    .D(controlled_buffer_1_out_2), .en(or_6_out), .clk(or_8_out), .Q(DATA_LATCH_H_q));  // open: clr
  buf or_8 (or_8_out, multiplexer_3_out[2]);  // OR_Gate
  Register #(.width(16)) SP (
    .D({controlled_buffer_1_out_2, controlled_buffer_1_out}), .clk(shift_register_2_p1[0]));  // open: en, Q, clr
  Register #(.width(16)) BP (
    .D({controlled_buffer_1_out_2, controlled_buffer_1_out}), .clk(shift_register_2_p1[0]));  // open: en, Q, clr
  Multiplexer #(.width(8)) multiplexer_4 (
    .in0(DATA_LATCH_L_q), .in1(DATA_LATCH_H_q), .out(multiplexer_4_out), .sel(or_6_out));
  Multiplexer #(.width(8)) multiplexer_5 (
    .in0(controlled_buffer_1_out), .in1(controlled_buffer_1_out_2), .out(multiplexer_5_out), .sel(or_6_out));
  assign multiplexer_5_out = MEM_O_EN ? DATA : 8'bz;  // Controlled_Buffer controlled_buffer_6
  Controlled_Buffer #(.width(8)) controlled_buffer_7 (.in(multiplexer_4_out), .out(DATA));  // open: en
  assign {controlled_buffer_1_out_2, controlled_buffer_1_out} = decoder_1_out3 ? {DATA_LATCH_H_q, DATA_LATCH_L_q} : 16'bz;  // Controlled_Buffer controlled_buffer_8
  RAM #(.addrWidth(16), .databus("bidir")) ram_1 (.oe(MEM_O_EN), .clk(MEM_CLK), .data(DATA));  // open: addr, we
endmodule
